# Fritzing sketch schematic (saved by Fritzing 0.9.9b)

parts:
  Raspberry_Pi_1 = Raspberry Pi 3 [part_number=RPI-3-V1.2]
  Part1 = Arduino Mega 2560 (Rev3)
  Part3 = I2C level shifter bidirectional
  U1 = 4-Channel 5v Relay Shield [package=relay-4ch5v10a]

nets:
  N1: Raspberry_Pi_1.3v3, Part3.LV
  GND: Raspberry_Pi_1.GND, Part1.GND, Part3.GND, U1.GND
  N2: Raspberry_Pi_1.GIPO15, Part3.LV1
  N3: Raspberry_Pi_1.GIPO14, Part3.LV2
  N4: Part1.D19/RX1, Part3.HV1
  N5: Part1.D18/TX1, Part3.HV2
  5V: Part1.5V, Part3.HV, U1.VCC
  N6: Part1.D2_PWM, U1.IN1
  N7: Part1.D3_PWM, U1.IN2
  N8: Part1.D4_PWM, U1.IN3
  N9: Part1.D22, U1.IN4

custom parts:
  4-Channel 5v Relay Shield: 4 Channel 5v Relay Shield w. 2x SPD-06VDC-SD-C
